// Logisim project Single Cycle Processor.circ as structural Verilog
module ALU (
  input  [1:0] Shift_Op,
  input  [31:0] A,
  input  Arithmetic_Op,
  input  [31:0] B,
  input  [1:0] Logical_Op,
  input  [1:0] ALU_Selection,
  output [31:0] ALU_result,
  output overflow,
  output [31:0] zero
);

  wire [31:0] adder_1_out, and_1_out, multiplexer_1_out, not_1_out, or_1_out, Shifter_data_out, xor_1_out,
       xor_2_out;
  wire [31:1] undriven;

  assign xor_1_out = B ^ {undriven, Arithmetic_Op};  // XOR_Gate xor_1, 32 bits wide
  assign and_1_out = A & B;  // AND_Gate and_1, 32 bits wide
  assign not_1_out = ~or_1_out;  // NOT_Gate not_1, 32 bits wide
  assign or_1_out = A | B;  // OR_Gate or_1, 32 bits wide
  assign xor_2_out = A ^ B;  // XOR_Gate xor_2, 32 bits wide
  Shifter Shifter (.Data(B), .Shift_amount(A[4:0]), .Shift_Op(Shift_Op), .Data_out(Shifter_data_out));
  Adder #(.width(32)) adder_1 (.a(A), .b(xor_1_out), .out(adder_1_out), .cin(Arithmetic_Op), .cout(overflow));
  Multiplexer #(.select(2), .width(32), .enable("false")) multiplexer_1 (
    .in0(and_1_out), .in1(or_1_out), .in2(not_1_out), .in3(xor_2_out), .out(multiplexer_1_out),
    .sel(Logical_Op));
  Multiplexer #(.select(2), .width(32), .enable("false")) multiplexer_2 (
    .in0(Shifter_data_out), .in2(adder_1_out), .in3(multiplexer_1_out), .out(ALU_result), .sel(ALU_Selection));  // open: in1
  assign zero = ~ALU_result;  // NOT_Gate not_2, 32 bits wide
  // Pins of 1 and 32 bits meet at {undriven, Arithmetic_Op}
endmodule

module Shifter (
  input  [31:0] Data,
  input  [4:0] Shift_amount,
  input  [1:0] Shift_Op,
  output [31:0] Data_out
);

  wire [31:0] shifter_1_out, shifter_2_out, shifter_3_out, shifter_4_out;

  Shifter_part #(.width(32)) shifter_1 (.in(Data), .\dist (Shift_amount), .out(shifter_1_out));
  Shifter_part #(.width(32), .shift("lr")) shifter_2 (.in(Data), .\dist (Shift_amount), .out(shifter_2_out));
  Shifter_part #(.width(32), .shift("ar")) shifter_3 (.in(Data), .\dist (Shift_amount), .out(shifter_3_out));
  Shifter_part #(.width(32), .shift("rr")) shifter_4 (.in(Data), .\dist (Shift_amount), .out(shifter_4_out));
  Multiplexer #(.select(2), .width(32), .enable("false")) multiplexer_1 (
    .in0(shifter_1_out), .in1(shifter_2_out), .in2(shifter_3_out), .in3(shifter_4_out), .out(Data_out),
    .sel(Shift_Op));
endmodule

module File_Register (
  input  [2:0] RA,
  input  [2:0] RB,
  input  [2:0] RW,
  input  [31:0] BusW,
  input  RegWrite,
  output [31:0] BusA,
  output [31:0] BusB
);

  wire and_1_out, and_2_out, and_3_out, and_4_out, and_5_out, and_6_out, and_7_out, and_8_out, clock_out,
       decoder_1_out0, decoder_1_out1, decoder_1_out2, decoder_1_out3, decoder_1_out4, decoder_1_out5,
       decoder_1_out6, decoder_1_out7, decoder_2_out0, decoder_2_out1, decoder_2_out2, decoder_2_out3,
       decoder_2_out4, decoder_2_out5, decoder_2_out6, decoder_2_out7, decoder_3_out0, decoder_3_out1,
       decoder_3_out2, decoder_3_out3, decoder_3_out4, decoder_3_out5, decoder_3_out6, decoder_3_out7;
  wire [31:0] register_1_q, register_2_q, register_3_q, register_4_q, register_5_q, register_6_q;

  Clock clock (.out(clock_out));
  Decoder #(.select(3), .enable("false")) decoder_1 (
    .out0(decoder_1_out0), .out1(decoder_1_out1), .out2(decoder_1_out2), .out3(decoder_1_out3),
    .out4(decoder_1_out4), .out5(decoder_1_out5), .out6(decoder_1_out6), .out7(decoder_1_out7), .sel(RW));
  Register #(.width(32)) register_1 (.D(BusW), .en(and_1_out), .Q(register_1_q), .clk(clock_out));  // open: clr
  and and_1 (and_1_out, decoder_1_out0, RegWrite);
  Register #(.width(32)) register_2 (.D(BusW), .en(and_2_out), .Q(register_2_q), .clk(clock_out));  // open: clr
  and and_2 (and_2_out, decoder_1_out1, RegWrite);
  Register #(.width(32)) register_3 (.D(BusW), .en(and_3_out), .Q(register_3_q), .clk(clock_out));  // open: clr
  and and_3 (and_3_out, decoder_1_out2, RegWrite);
  Register #(.width(32)) register_4 (.D(BusW), .en(and_4_out), .Q(register_4_q), .clk(clock_out));  // open: clr
  and and_4 (and_4_out, decoder_1_out3, RegWrite);
  Register #(.width(32)) register_5 (.D(BusW), .en(and_5_out), .Q(register_5_q), .clk(clock_out));  // open: clr
  and and_5 (and_5_out, decoder_1_out4, RegWrite);
  Register #(.width(32)) register_6 (.D(BusW), .en(and_6_out), .Q(register_6_q), .clk(clock_out));  // open: clr
  and and_6 (and_6_out, decoder_1_out5, RegWrite);
  Register #(.width(32)) register_7 (.D(BusW), .en(and_7_out), .Q(BusA), .clk(clock_out));  // open: clr
  and and_7 (and_7_out, decoder_1_out6, RegWrite);
  Register #(.width(32)) register_8 (.D(BusW), .en(and_8_out), .Q(BusA), .clk(clock_out));  // open: clr
  and and_8 (and_8_out, decoder_1_out7, RegWrite);
  Decoder #(.select(3), .enable("false")) decoder_2 (
    .out0(decoder_2_out0), .out1(decoder_2_out1), .out2(decoder_2_out2), .out3(decoder_2_out3),
    .out4(decoder_2_out4), .out5(decoder_2_out5), .out6(decoder_2_out6), .out7(decoder_2_out7), .sel(RA));
  assign BusA = decoder_2_out7 ? register_1_q : 32'bz;  // Controlled_Buffer controlled_buffer_1
  assign BusA = decoder_2_out6 ? register_2_q : 32'bz;  // Controlled_Buffer controlled_buffer_2
  assign BusA = decoder_2_out5 ? register_3_q : 32'bz;  // Controlled_Buffer controlled_buffer_3
  assign BusA = decoder_2_out4 ? register_4_q : 32'bz;  // Controlled_Buffer controlled_buffer_4
  assign BusA = decoder_2_out3 ? register_5_q : 32'bz;  // Controlled_Buffer controlled_buffer_5
  assign BusA = decoder_2_out2 ? register_6_q : 32'bz;  // Controlled_Buffer controlled_buffer_6
  assign BusA = decoder_2_out1 ? BusA : 32'bz;  // Controlled_Buffer controlled_buffer_7
  assign BusA = decoder_2_out0 ? BusA : 32'bz;  // Controlled_Buffer controlled_buffer_8
  Decoder #(.select(3), .enable("false")) decoder_3 (
    .out0(decoder_3_out0), .out1(decoder_3_out1), .out2(decoder_3_out2), .out3(decoder_3_out3),
    .out4(decoder_3_out4), .out5(decoder_3_out5), .out6(decoder_3_out6), .out7(decoder_3_out7), .sel(RB));
  assign BusB = decoder_3_out7 ? register_1_q : 32'bz;  // Controlled_Buffer controlled_buffer_9
  assign BusB = decoder_3_out6 ? register_2_q : 32'bz;  // Controlled_Buffer controlled_buffer_10
  assign BusB = decoder_3_out5 ? register_3_q : 32'bz;  // Controlled_Buffer controlled_buffer_11
  assign BusB = decoder_3_out4 ? register_4_q : 32'bz;  // Controlled_Buffer controlled_buffer_12
  assign BusB = decoder_3_out3 ? register_5_q : 32'bz;  // Controlled_Buffer controlled_buffer_13
  assign BusB = decoder_3_out2 ? register_6_q : 32'bz;  // Controlled_Buffer controlled_buffer_14
  assign BusB = decoder_3_out1 ? BusA : 32'bz;  // Controlled_Buffer controlled_buffer_15
  assign BusB = decoder_3_out0 ? BusA : 32'bz;  // Controlled_Buffer controlled_buffer_16
endmodule
